# Fritzing sketch LiDAR-pcb (saved by Fritzing 0.9.3b)
circuit board: 5.1cm x 5cm
breadboards: 1

parts:
  Arduino_Nano = Arduino Nano (Rev3.0) (ICSP)
  J2 = screw terminal, 3 pins
  J3 = screw terminal, 4 pins
  C2 = Electrolytic Capacitor [capacitance=100µF package="100 mil [THT, electrolytic]"]
  J5 = screw terminal, 5 pins
  C1 = Electrolytic Capacitor [capacitance=1µF package="100 mil [THT, electrolytic]"]
  Q1 = PNP-Transistor [package="TO92 [THT]"]
  C4 = Ceramic Capacitor [capacitance=100nF package="100 mil [THT, multilayer]"]
  C3 = Ceramic Capacitor [capacitance=100nF package="100 mil [THT, multilayer]"]
  J4 = Screw terminal - 2 pins [package=THT]
  J1 = Screw terminal - 2 pins [package=THT]
  A4988 = Pololu A4988 [package=SO16]

nets:
  N1: Arduino_Nano.GND, J2.pin1, J5.pin3, C1.-, J1.pin1, A4988.GND#8
  N2: Arduino_Nano.D2, A4988.DIR
  N3: Arduino_Nano.D3, A4988.STEP
  N4: Arduino_Nano.D4, A4988.ENABLE
  N5: Arduino_Nano.D5, J2.pin2
  5V: Arduino_Nano.5V, J2.pin3, C1.+, J1.pin2, A4988.VDD
  N6: Arduino_Nano.A5, Arduino_Nano.A4, J5.pin4, J5.pin5
  N7: J3.pin1, A4988.2B
  N8: J3.pin2, A4988.2A
  N9: J3.pin3, A4988.1A
  N10: J3.pin4, A4988.1B
  N11: C2.-, J5.pin1, Q1.B, C4.1, C3.0, J4.pin1, A4988.GND#14
  N12: C2.+, Q1.C, C3.1, J4.pin2, A4988.VMOT
  N13: J5.pin2, Q1.E, C4.0
  N14: A4988.RESET, A4988.SLEEP
